# Fritzing sketch schematic (saved by Fritzing 0.7.11b)
breadboards: 1

parts:
  Componente1 = Thumb Joystick
  S2 = Pushbutton [package="[THT]"]
  S3 = Pushbutton [package="[THT]"]
  U1 = atmega168 [package=dip]
  XTAL1 = Crystal [frequency="16 Mhz" package=THT]
  C1 = Ceramic Disk Capacitor [package=THT]
  C2 = Ceramic Disk Capacitor [package=THT]

nets:
  GND: Componente1.GND
  N1: S2.Pin_1, S2.Pin_2
  N2: S2.Pin_3, S2.Pin_4
  N3: S3.Pin_1, S3.Pin_2
  N4: S3.Pin_3, S3.Pin_4
  N5: U1.XLAT1, XTAL1.pin_0, C1.pin_1
  N6: U1.XLAT2, XTAL1.pin_1, C2.pin_1
  N7: C1.pin_0, C2.pin_0
